# Fritzing sketch schemat (saved by Fritzing 0.9.3b)
breadboards: 2

parts:
  Part1 = Arduino Nano (Rev3.0)  # not connected
  S1 = Reed switch [package=THT]
  C1 = Electrolytic Capacitor [capacitance=1µF package="100 mil [THT, electrolytic]"]

nets:
  N1: S1.pin_1, C1.+
  N2: S1.pin_2, C1.-
