# Fritzing sketch schemat (saved by Fritzing 0.9.3b)

parts:
  Pro_Micro1 = Pro Micro
  OLED_I2C1 = OLED 128x64 I2C Monochrome Display
  Part1 = KY-003 Hall Magnetic Sensor Module [package="Breakout board"]

nets:
  N1: Pro_Micro1.TX1, Part1.S
  N2: Pro_Micro1.GND#3, OLED_I2C1.GND
  N3: Pro_Micro1.GND#4, Part1.-
  N4: Pro_Micro1.D2, OLED_I2C1.SDA
  N5: Pro_Micro1.D3, OLED_I2C1.SCK
  VCC: Pro_Micro1.VCC, OLED_I2C1.VDD, Part1.Vin

custom parts:
  Pro Micro: The SparkFun Pro Micro is a complete USB-based microcontoller development system, in a very small footprint, capable of implementing many types of projects. All programming can be done via the USB port.
  KY-003 Hall Magnetic Sensor Module: KEYES KY-003 Arduino Hall Magnetic Sensor Module is a switch that will turn on/off in the presence of a magnetic field.
